// Logisim project v1.circ as structural Verilog
module ALU (
  input  [7:0] A,
  input  [7:0] B,
  input  [2:0] ALUop,
  output out_4,
  output out_5,
  output ZF,
  output [7:0] F
);

  wire [7:0] adder_1_out, and_1_out, nor_1_out, or_1_out, subtractor_1_out;
  wire [15:0] shifter_1_out, shifter_2_out;

  Adder adder_1 (.a(A), .b(B), .out(adder_1_out), .cin(1'b0), .cout(out_4));
  Subtractor subtractor_1 (.a(A), .b(B), .out(subtractor_1_out), .bin(1'b0), .bout(out_5));
  assign or_1_out = A | B;  // OR_Gate or_1, 8 bits wide
  assign and_1_out = A & B;  // AND_Gate and_1, 8 bits wide
  assign nor_1_out = ~(A | B);  // NOR_Gate nor_1, 8 bits wide
  Shifter #(.width(16)) shifter_1 (.in({{8{1'b0}}, A}), .\dist (B[3:0]), .out(shifter_1_out));
  Shifter #(.width(16), .shift("lr")) shifter_2 (.in({{8{1'b0}}, A}), .\dist (B[3:0]), .out(shifter_2_out));
  Multiplexer #(.select(3), .width(8), .enable("false")) multiplexer_1 (
    .in0(adder_1_out), .in1(subtractor_1_out), .in2(or_1_out), .in3(and_1_out), .in4(nor_1_out),
    .in5(shifter_1_out[7:0]), .in6(shifter_2_out[7:0]), .in7({8{1'b0}}), .out(F), .sel(ALUop));
  nor nor_2 (ZF, F[0], F[1], F[2], F[3], F[4], F[5], F[6], F[7]);
endmodule

module Registers (
  input  [3:0] READ_REGISTER_1,
  input  [3:0] READ_REGISTER_2,
  input  [3:0] WRITE_REGISTER,
  input  [7:0] WRITE_DATA,
  input  CLK,
  input  REG_WRITE,
  output [7:0] READ_DATA_1,
  output [7:0] READ_DATA_2
);

  wire demultiplexer_1_out0, demultiplexer_1_out1, demultiplexer_1_out2, demultiplexer_1_out3,
       demultiplexer_1_out4, demultiplexer_1_out5, demultiplexer_1_out6;
  wire [7:0] SP_q, t0_q, t1_q, t2_q, t3_q, t4_q, ZERO_q;

  Demultiplexer #(.select(4), .disabled(0)) demultiplexer_1 (
    .out0(demultiplexer_1_out0), .out1(demultiplexer_1_out1), .out2(demultiplexer_1_out2),
    .out3(demultiplexer_1_out3), .out4(demultiplexer_1_out4), .out5(demultiplexer_1_out5),
    .out6(demultiplexer_1_out6), .in(1'b1), .sel(WRITE_REGISTER), .en(REG_WRITE));  // open: out7, out8, out9, out10, out11, out12, out13, out14, out15
  Register t0 (.D(WRITE_DATA), .en(demultiplexer_1_out0), .Q(t0_q), .clk(CLK));  // open: clr
  Register t1 (.D(WRITE_DATA), .en(demultiplexer_1_out1), .Q(t1_q), .clk(CLK));  // open: clr
  Register t2 (.D(WRITE_DATA), .en(demultiplexer_1_out2), .Q(t2_q), .clk(CLK));  // open: clr
  Register t3 (.D(WRITE_DATA), .en(demultiplexer_1_out3), .Q(t3_q), .clk(CLK));  // open: clr
  Register t4 (.D(WRITE_DATA), .en(demultiplexer_1_out4), .Q(t4_q), .clk(CLK));  // open: clr
  Register ZERO (.D(WRITE_DATA), .en(demultiplexer_1_out5), .Q(ZERO_q), .clk(CLK));  // open: clr
  Register SP (.D(WRITE_DATA), .en(demultiplexer_1_out6), .Q(SP_q), .clk(CLK));  // open: clr
  Multiplexer #(.select(4), .width(8), .enable("false")) multiplexer_1 (
    .in0(t0_q), .in1(t1_q), .in2(t2_q), .in3(t3_q), .in4(t4_q), .in5(ZERO_q), .in6(SP_q), .out(READ_DATA_1),
    .sel(READ_REGISTER_1));  // open: in7, in8, in9, in10, in11, in12, in13, in14, in15
  Multiplexer #(.select(4), .width(8), .enable("false")) multiplexer_2 (
    .in0(t0_q), .in1(t1_q), .in2(t2_q), .in3(t3_q), .in4(t4_q), .in5(ZERO_q), .in6(SP_q), .out(READ_DATA_2),
    .sel(READ_REGISTER_2));  // open: in7, in8, in9, in10, in11, in12, in13, in14, in15
endmodule

module Instruction_Memory (
  input  [7:0] READ_ADDRESS,
  output [19:0] INSTRUCTION
);

  ROM #(.dataWidth(20)) rom_1 (.addr(READ_ADDRESS), .data(INSTRUCTION));  // open: sel

  // Notes on the sheet:
  //   contents of rom_1 (hex, n*v repeats v):
  //   1aaff 100df 321 abcd abcde 248*0 fffda fffee fffdd
endmodule

module Data_Memory (
  input  [7:0] WRITE_DATA,
  input  MEM_WRITE,
  input  [7:0] ADDRESS,
  input  CLK,
  output [7:0] OUTPUT
);

  wire not_1_out;

  assign OUTPUT = MEM_WRITE ? WRITE_DATA : 8'bz;  // Controlled_Buffer controlled_buffer_1
  not not_1 (not_1_out, MEM_WRITE);
  RAM ram_1 (.addr(ADDRESS), .data(OUTPUT), .clk(CLK), .ld(not_1_out));  // open: sel, clr
endmodule

module Control_Unit (
  input  [3:0] INSTRUCTION,
  output ALU_OP_0,
  output ALU_OP_1,
  output ALU_OP_2,
  output JMP,
  output BRANCH,
  output MEM_WRITE,
  output MEM_READ,
  output REG_WRITE,
  output MEM_2_REG,
  output ALU_SRC,
  output REG_DEST
);

  wire [15:15] rom_1_data;

  ROM #(.addrWidth(4), .dataWidth(16)) rom_1 (
    .addr(INSTRUCTION),
    .data({{5{rom_1_data[15]}}, REG_DEST, ALU_SRC, MEM_2_REG, REG_WRITE, MEM_READ, MEM_WRITE, BRANCH, JMP, ALU_OP_2, ALU_OP_1, ALU_OP_0}));  // open: sel
  // also tied to GND on the sheet: rom_1_data[15]

  // Notes on the sheet:
  //   contents of rom_1 (hex, n*v repeats v):
  //   71f 480 1482 1c85 2283 2d01 3483 3a82 4486 4d11 53c0 5a81 6481 6f20 7484 7a80
endmodule
