// Logisim project v1 (1).circ as structural Verilog
module main (
  output [19:0] INSTRUCTION,
  output out_2,
  output [7:0] rd1,
  output [7:0] WD,
  output [7:0] rd2,
  output [7:0] t0,
  output [7:0] t1,
  output [7:0] t2,
  output [7:0] t3,
  output [7:0] t4,
  output [7:0] t5,
  output [7:0] zero,
  output [7:0] sp
);

  wire alu_1_out_4, clock_1_out, undriven;
  wire [3:0] control_unit_1_alu_op_0, id_ex_1_p7;
  wire [7:0] adder_1_out, PC_q, registers_1_read_data_1, registers_1_read_data_2;
  wire [19:0] if_id_1_output;

  Register PC (.D(adder_1_out), .Q(PC_q), .clk(clock_1_out));  // open: en, clr
  Adder adder_1 (.a(PC_q), .b(8'h1), .out(adder_1_out), .cin(1'b0));  // open: cout
  Clock clock_1 (.out(clock_1_out));
  ROM #(.dataWidth(20)) rom_1 (.addr(PC_q), .data(INSTRUCTION));  // open: sel
  IF_ID if_id_1 (.Data(INSTRUCTION), .ENABLE(1'b1), .CLK(clock_1_out), .Output(if_id_1_output));
  Control_Unit control_unit_1 (
    .INSTRUCTION(if_id_1_output[19:16]), .ALU_OP_0(control_unit_1_alu_op_0[0]),
    .ALU_OP_1(control_unit_1_alu_op_0[1]), .ALU_OP_2(control_unit_1_alu_op_0[2]),
    .REG_WRITE(control_unit_1_alu_op_0[3]));  // open: JMP, BRANCH, MEM_WRITE, MEM_READ, MEM_2_REG, ALU_SRC, REG_DEST, SHIFT, Branch_N
  Registers registers_1 (
    .READ_REGISTER_1(if_id_1_output[15:12]), .READ_REGISTER_2(if_id_1_output[11:8]), .WRITE_DATA(WD),
    .REG_WRITE(undriven), .READ_DATA_1(registers_1_read_data_1), .READ_DATA_2(registers_1_read_data_2),
    .CLK(clock_1_out), .t0(t0), .t1(t1), .t2(t2), .t3(t3), .t4(t4), .zero(zero), .sp(sp), .t5(t5));  // open: WRITE_REGISTER
  // ID_EX id_ex_1: pin names not known; wires that end beside it: control_unit_1_alu_op_0, registers_1_read_data_1, registers_1_read_data_2, if_id_1_output[7:4], 1'b1, clock_1_out, id_ex_1_p7, rd1, rd2
  ALU alu_1 (.A(rd1), .B(rd2), .ALUop(id_ex_1_p7[2:0]), .ZF(out_2), .F(WD), .out_4(alu_1_out_4));  // open: out_5

  // Notes on the sheet:
  //   READ ADDRESS
endmodule

module ALU (
  input  [7:0] A,
  input  [7:0] B,
  input  [2:0] ALUop,
  output out_4,
  output out_5,
  output ZF,
  output [7:0] F
);

  wire [7:0] adder_1_out, and_1_out, nor_1_out, or_1_out, subtractor_1_out;
  wire [15:0] shifter_1_out, shifter_2_out;

  Adder adder_1 (.a(A), .b(B), .out(adder_1_out), .cin(1'b0), .cout(out_4));
  Subtractor subtractor_1 (.a(A), .b(B), .out(subtractor_1_out), .bin(1'b0), .bout(out_5));
  assign or_1_out = A | B;  // OR_Gate or_1, 8 bits wide
  assign and_1_out = A & B;  // AND_Gate and_1, 8 bits wide
  assign nor_1_out = ~(A | B);  // NOR_Gate nor_1, 8 bits wide
  Shifter #(.width(16)) shifter_1 (.in({{8{1'b0}}, A}), .\dist (B[3:0]), .out(shifter_1_out));
  Shifter #(.width(16), .shift("lr")) shifter_2 (.in({{8{1'b0}}, A}), .\dist (B[3:0]), .out(shifter_2_out));
  Multiplexer #(.select(3), .width(8), .enable("false")) multiplexer_1 (
    .in0(adder_1_out), .in1(subtractor_1_out), .in2(or_1_out), .in3(and_1_out), .in4(nor_1_out),
    .in5(shifter_1_out[7:0]), .in6(shifter_2_out[7:0]), .in7({8{1'b0}}), .out(F), .sel(ALUop));
  nor nor_2 (ZF, F[0], F[1], F[2], F[3], F[4], F[5], F[6], F[7]);
endmodule

module Registers (
  input  [3:0] READ_REGISTER_1,
  input  [3:0] READ_REGISTER_2,
  input  [3:0] WRITE_REGISTER,
  input  [7:0] WRITE_DATA,
  input  CLK,
  input  REG_WRITE,
  output [7:0] t0,
  output [7:0] t1,
  output [7:0] t2,
  output [7:0] READ_DATA_1,
  output [7:0] t3,
  output [7:0] t4,
  output [7:0] zero,
  output [7:0] sp,
  output [7:0] t5,
  output [7:0] READ_DATA_2
);

  wire demultiplexer_1_out0, demultiplexer_1_out1, demultiplexer_1_out2, demultiplexer_1_out3,
       demultiplexer_1_out4, demultiplexer_1_out5, demultiplexer_1_out6, demultiplexer_1_out7;

  Demultiplexer #(.select(4), .disabled(0)) demultiplexer_1 (
    .out0(demultiplexer_1_out0), .out1(demultiplexer_1_out1), .out2(demultiplexer_1_out2),
    .out3(demultiplexer_1_out3), .out4(demultiplexer_1_out4), .out5(demultiplexer_1_out5),
    .out6(demultiplexer_1_out6), .out7(demultiplexer_1_out7), .in(1'b1), .sel(WRITE_REGISTER), .en(REG_WRITE));  // open: out8, out9, out10, out11, out12, out13, out14, out15
  Register u_t0 (.D(WRITE_DATA), .en(demultiplexer_1_out0), .Q(t0), .clk(CLK));  // open: clr
  Register u_t1 (.D(WRITE_DATA), .en(demultiplexer_1_out1), .Q(t1), .clk(CLK));  // open: clr
  Register u_t2 (.D(WRITE_DATA), .en(demultiplexer_1_out2), .Q(t2), .clk(CLK));  // open: clr
  Register u_t3 (.D(WRITE_DATA), .en(demultiplexer_1_out3), .Q(t3), .clk(CLK));  // open: clr
  Register u_t4 (.D(WRITE_DATA), .en(demultiplexer_1_out4), .Q(t4), .clk(CLK));  // open: clr
  Register u_ZERO (.D(WRITE_DATA), .en(demultiplexer_1_out5), .Q(zero));  // open: clk, clr
  Register u_SP (.D(WRITE_DATA), .en(demultiplexer_1_out6), .Q(sp), .clk(CLK));  // open: clr
  Register u_t5 (.D(WRITE_DATA), .en(demultiplexer_1_out7), .Q(t5), .clk(CLK));  // open: clr
  Multiplexer #(.select(4), .width(8), .enable("false")) multiplexer_1 (
    .in0(t0), .in1(t1), .in2(t2), .in3(t3), .in4(t4), .in5(zero), .in6(sp), .in7(t5), .out(READ_DATA_1),
    .sel(READ_REGISTER_1));  // open: in8, in9, in10, in11, in12, in13, in14, in15
  Multiplexer #(.select(4), .width(8), .enable("false")) multiplexer_2 (
    .in0(t0), .in1(t1), .in2(t2), .in3(t3), .in4(t4), .in5(zero), .in6(sp), .in7(t5), .out(READ_DATA_2),
    .sel(READ_REGISTER_2));  // open: in8, in9, in10, in11, in12, in13, in14, in15
endmodule

module Data_Memory (
  input  [7:0] ADDRESS,
  input  [7:0] WRITE_DATA,
  input  MEM_WRITE,
  input  MEM_READ,
  input  CLK,
  output [7:0] READ_DATA
);

  RAM #(.bus("separate")) ram_1 (
    .addr(ADDRESS), .din(WRITE_DATA), .data(READ_DATA), .str(MEM_WRITE), .clk(CLK), .ld(MEM_READ));  // open: sel, clr

  // Notes on the sheet:
  //   DATA MEMORY
endmodule

module Control_Unit (
  input  [3:0] INSTRUCTION,
  output ALU_OP_0,
  output ALU_OP_1,
  output ALU_OP_2,
  output JMP,
  output BRANCH,
  output MEM_WRITE,
  output MEM_READ,
  output REG_WRITE,
  output MEM_2_REG,
  output ALU_SRC,
  output REG_DEST,
  output SHIFT,
  output Branch_N
);

  wire [15:15] rom_1_data;

  ROM #(.addrWidth(4), .dataWidth(16)) rom_1 (
    .addr(INSTRUCTION),
    .data({{3{rom_1_data[15]}}, Branch_N, SHIFT, REG_DEST, ALU_SRC, MEM_2_REG, REG_WRITE, MEM_READ, MEM_WRITE, BRANCH, JMP, ALU_OP_2, ALU_OP_1, ALU_OP_0}));  // open: sel
  // also tied to GND on the sheet: rom_1_data[15]

  // Notes on the sheet:
  //   contents of rom_1 (hex, n*v repeats v):
  //   71f 480 482 e85 283 1501 483 282 e86 511 3c0 281 481 720 484 280
endmodule

module IF_ID (
  input  [19:0] Data,
  input  ENABLE,
  input  CLK,
  output [19:0] Output
);

  Register #(.width(20)) register_1 (.D(Data), .en(ENABLE), .Q(Output), .clk(CLK));  // open: clr
endmodule

module ID_EX (
  input  [3:0] CNTRL,
  input  [7:0] RD1,
  input  [7:0] RD2,
  input  [3:0] WR,
  input  CLK,
  input  ENABLE,
  output [3:0] CNTRL_OUT,
  output [7:0] RD1_2,
  output [7:0] RD1_3,
  output [3:0] WR_2
);

  Register #(.width(4)) _4_bit (.D(CNTRL), .en(ENABLE), .Q(CNTRL_OUT), .clk(CLK));  // open: clr
  Register _8_bit (.D(RD1), .en(ENABLE), .Q(RD1_2), .clk(CLK));  // open: clr
  Register _8_bit_2 (.D(RD2), .en(ENABLE), .Q(RD1_3), .clk(CLK));  // open: clr
  Register #(.width(4)) _4_bit_2 (.D(WR), .en(ENABLE), .Q(WR_2), .clk(CLK));  // open: clr
endmodule

module EX_MEM (
  input  [7:0] ALU,
  input  RW,
  input  WR,
  input  CLK,
  input  ENABLE,
  output [7:0] ALU_2,
  output RW_2,
  output WR_2
);

  Register u_ALU (.D(ALU), .en(ENABLE), .Q(ALU_2), .clk(CLK));  // open: clr
  Register #(.width(1)) u_RW (.D(RW), .en(ENABLE), .Q(RW_2), .clk(CLK));  // open: clr
  Register #(.width(1)) u_WR (.D(WR), .en(ENABLE), .Q(WR_2), .clk(CLK));  // open: clr
endmodule
